# Fritzing sketch Fritzing Sketch Source File (saved by Fritzing 0.9.3b)
breadboards: 1

parts:
  Part1 = Arduino Uno (Rev3)
  J1 = Basic Servo
  LCM1602_IIC1 = LCM1602 IIC [part_number="LCM1602 IIC" chip_label="LCM1602 IIC" package="DIP (Dual Inline) [THT]"]
  U1 = LCD-16X2 [package=lcd-16x2]
  VCC1 = Battery block 9V
  Keypad4x1 = Keypad Membran 4x4

nets:
  N1: Part1.D8, Keypad4x1.Pin3
  N2: Part1.D9_PWM, Keypad4x1.Pin4
  N3: Part1.D10_PWM/SS, J1.pulse
  GND: Part1.GND, J1.gnd, LCM1602_IIC1.GND, VCC1.-
  N4: Part1.A4/SDA, LCM1602_IIC1.SDA
  N5: Part1.A5/SCL, LCM1602_IIC1.SCL
  N6: Part1.D2, Keypad4x1.Pin5
  N7: Part1.D3_PWM, Keypad4x1.Pin6
  N8: Part1.D4, Keypad4x1.Pin7
  N9: Part1.D5_PWM, Keypad4x1.Pin8
  N10: Part1.D6_PWM, Keypad4x1.Pin1
  N11: Part1.D7, Keypad4x1.Pin2
  5V: Part1.5V, LCM1602_IIC1.VCC
  N12: J1.vcc, VCC1.+
  N13: LCM1602_IIC1.VSS, U1.K
  N14: LCM1602_IIC1.VDD, U1.A
  N15: LCM1602_IIC1.V0, U1.DB7
  N16: LCM1602_IIC1.RS, U1.DB6
  N17: LCM1602_IIC1.RW, U1.DB5
  N18: LCM1602_IIC1.E, U1.DB4
  N19: LCM1602_IIC1.D0, U1.DB3
  N20: LCM1602_IIC1.D1, U1.DB2
  N21: LCM1602_IIC1.D2, U1.DB1
  N22: LCM1602_IIC1.D3, U1.DB0
  N23: LCM1602_IIC1.D4, U1.E
  N24: LCM1602_IIC1.D5, U1.R_W
  N25: LCM1602_IIC1.D6, U1.RS
  N26: LCM1602_IIC1.D7, U1.VO
  N27: LCM1602_IIC1.A, U1.VDD
  N28: LCM1602_IIC1.K, U1.VSS

notes:
  GND - Green
  5VC - Red
  GPIO - Blue
  Developed By Web Dev Fusion
  www.webdevfusion.com

custom parts:
  LCM1602 IIC: I2C-Module to use a 1602 or 2004 LCD on with the wire.h libory Serial LCD Modul
  Keypad Membran 4x4: Membrane Keypad 4x4 Matrix
